# Fritzing sketch Debounce with Schmitt-Trigger (saved by Fritzing 0.9.3b)
breadboards: 1

parts:
  IC1 = Hex Inverter Schmitt Trigger SN74HC14 [package="DIP (Dual Inline)"]
  R1 = Resistor [tolerance=±5% resistance=10k package=THT]
  S1 = Pushbutton [package="[THT]"]
  C1 = Ceramic Capacitor [capacitance=0.1µF package="100 mil [THT, multilayer]"]
  Part1 = Arduino Uno (Rev3)
  R2 = Resistor [tolerance=±5% resistance=10k package=THT]

nets:
  N1: IC1.1A, R1.Pin_1, C1.1
  N2: IC1.1Y, Part1.D3_PWM
  GND: IC1.GND, S1.Pin_3, S1.Pin_4, C1.0, Part1.GND
  VCC: IC1.VCC, Part1.5V, R2.Pin_1
  N3: R1.Pin_0, S1.Pin_1, S1.Pin_2, R2.Pin_0
