# Fritzing sketch RC_Debounce (saved by Fritzing 0.9.3b)
breadboards: 1

parts:
  R1 = Resistor [tolerance=±5% resistance=1k package=THT]
  C1 = Electrolytic Capacitor [capacitance=1µF package="100 mil [THT, electrolytic]"]
  S1 = Pushbutton [package="[THT]"]
  R2 = Resistor [tolerance=±5% resistance=1k package=THT]
  Part1 = Arduino Uno (Rev3)

nets:
  N1: R1.Pin_0, C1.+, S1.Pin_1, S1.Pin_2, Part1.D3_PWM
  N2: R1.Pin_1, C1.-, Part1.GND
  N3: S1.Pin_3, S1.Pin_4, R2.Pin_1
  N4: R2.Pin_0, Part1.5V
