# Fritzing sketch Hbridge IC (saved by Fritzing 0.9.3b)
breadboards: 1

parts:
  IC1 = H-Bridge [package=THT]
  Power_plug1 = Power plug
  Part1 = Arduino Uno (Rev3)
  M1 = DC Motor
  M2 = DC Motor

nets:
  N1: IC1.1_2EN, IC1.VCC1, Part1.5V
  N2: IC1.1A, Part1.D5_PWM
  N3: IC1.1Y, M1.pin_2
  GND: IC1.GND1, IC1.GND2, IC1.GND3, IC1.GND4, Power_plug1.GND, Part1.GND
  N4: IC1.2Y, M1.pin_1
  N5: IC1.2A, Part1.D6_PWM
  N6: IC1.VCC2, Power_plug1.VCC
  N7: IC1.3A, Part1.D10_PWM/SS
  N8: IC1.3Y, M2.pin_2
  N9: IC1.4Y, M2.pin_1
  N10: IC1.4A, Part1.D9_PWM
