# Fritzing sketch HBridge (saved by Fritzing 0.9.3b)
breadboards: 1

parts:
  Q1 = NPN-Transistor [package="TO92 [THT]"]
  Q2 = NPN-Transistor [package="TO92 [THT]"]
  R1 = Resistor [tolerance=±5% resistance=220 package=THT]
  R2 = Resistor [tolerance=±5% resistance=220 package=THT]
  Q4 = PNP-Transistor [package="TO92 [THT]"]
  R3 = Resistor [tolerance=±5% resistance=220 package=THT]
  R4 = Resistor [tolerance=±5% resistance=220 package=THT]
  D1 = Rectifier Diode [part_number=1N4001 package="300 mil [THT]"]
  D2 = Rectifier Diode [part_number=1N4001 package="300 mil [THT]"]
  D3 = Rectifier Diode [part_number=1N4001 package="300 mil [THT]"]
  Power_plug1 = Power plug
  M1 = DC Motor
  Part1 = Arduino Uno (Rev3)
  D4 = Rectifier Diode [part_number=1N4001 package="300 mil [THT]"]
  Q3 = PNP-Transistor [package="TO92 [THT]"]

nets:
  GND: Q1.E, Q2.E, D3.anode, Power_plug1.GND, Part1.GND, D4.anode
  N1: Q1.B, R4.Pin_0
  N2: Q1.C, D1.anode, M1.pin_2, D4.cathode, Q3.C
  N3: Q2.B, R3.Pin_0
  N4: Q2.C, Q4.C, D2.anode, D3.cathode, M1.pin_1
  N5: R1.Pin_0, Q4.B
  N6: R1.Pin_1, R3.Pin_1, Part1.D10_PWM/SS
  N7: R2.Pin_0, Q3.B
  N8: R2.Pin_1, R4.Pin_1, Part1.D9_PWM
  N9: Q4.E, D1.cathode, D2.cathode, Power_plug1.VCC, Q3.E

notes:
  Because all these parts have bendable legs, You will *NOT* need this many routes and wires.
  Pick transistors and flyback diodes that work best for your load.
  [example:
  NPN Transistor: BC337
  PNP Transistor: BC327
  Diodes: 1N4007
  ]
