# Fritzing sketch HBridge_Quick (saved by Fritzing 0.9.3b)
breadboards: 1

parts:
  Q1 = NPN-Transistor [package="TO92 [THT]"]
  Q2 = NPN-Transistor [package="TO92 [THT]"]
  R2 = Resistor [tolerance=±5% resistance=220 package=THT]
  Q4 = PNP-Transistor [package="TO92 [THT]"]
  M1 = DC Motor
  Part1 = Arduino Uno (Rev3)
  Q3 = PNP-Transistor [package="TO92 [THT]"]
  R3 = Resistor [tolerance=±5% resistance=220 package=THT]
  C1 = Electrolytic Capacitor [capacitance=10µF package="100 mil [THT, electrolytic]"]

nets:
  N1: Q1.E, Q2.E, Part1.GND, C1.-
  N2: Q1.B, R2.Pin_0, Q3.B
  N3: Q1.C, M1.pin_1, Q3.C
  N4: Q2.B, Q4.B, R3.Pin_0
  N5: Q2.C, Q4.C, M1.pin_2
  N6: R2.Pin_1, Part1.D9_PWM
  N7: Q4.E, Part1.VIN, Q3.E, C1.+
  N8: Part1.D10_PWM/SS, R3.Pin_1

notes:
  Because all these parts have bendable legs, You will *NOT* need this many routes and wires.
  Pick transistors that work best for your load.
  [example:
  NPN Transistor: TIP120
  PNP Transistor: TIP125
  ]
  You can use Vin on most controllers to access the power source. Just put a capacitor here to try and prevent current surges.
