# Fritzing sketch gpio_ruggedizer (saved by Fritzing 0.9.3b)
breadboards: 1

parts:
  D1 = Zener Diode [part_number=1N4732A breakdown_voltage=5.1V package="Melf DO-213 AB [SMD]"]
  part = Arduino Uno (Rev3)
  R1 = Temperature Sensor (Thermistor) [thermistor_type=NTC package=THT]
  J1 = female pin header, 1 pin [form="♀ (female)"]

nets:
  N1: D1.cathode, part.D7, R1.pin_0
  N2: D1.anode, part.GND
  New gpio terminal: R1.pin_1, J1.pin1
