# Fritzing sketch Const_LVR (saved by Fritzing 0.9.3b)
breadboards: 1

parts:
  BAT1 = BC9VPC [package=bc9vpc]
  C2 = Ceramic Capacitor [capacitance="100 nF" package="1206 [SMD, multilayer]"]
  C3 = Electrolytic Capacitor [capacitance=10µF package="1010 [SMD, electrolytic]"]
  C4 = Electrolytic Capacitor [capacitance=10µF package="1010 [SMD, electrolytic]"]
  IC1 = Voltage Regulator [package=78xxl]
  C1 = Ceramic Capacitor [capacitance=330nF package="1206 [SMD, multilayer]"]

nets:
  N1: BAT1.V+, C3.+, IC1.IN, C1.1
  GND: BAT1.V-, C2.0, C3.-, C4.-, IC1.GND, C1.0
  5V: C2.1, C4.+, IC1.OUT

notes:
  Place ceramic capacitors as close to the regulator as possible
  Electrolytic Capacitors on the input and output voltages aren't required, but are best practice
