# Fritzing sketch Var_LVR (saved by Fritzing 0.9.3b)
breadboards: 1

parts:
  R1 = Trimmer Potentiometer [maximum_resistance=10kΩ package=THT]
  C3 = Electrolytic Capacitor [capacitance=10μF package="0605 [SMD, electrolytic]"]
  R2 = Resistor [tolerance=±5% resistance=330 package=THT]
  VCC1 = Battery block 9V
  C5 = Capacitor [package=cap-pth-large]
  IC1 = Voltage Regulator [package=to220-adj]

nets:
  N1: R1.leg1, R1.wiper, R2.Pin_0
  N2: R1.leg2, VCC1.-, C5.1, IC1.ADJ
  GND: C3.-
  12V: C3.+, R2.Pin_1, IC1.OUT
  N3: VCC1.+, C5.2, IC1.IN
