# Fritzing sketch circuit (saved by Fritzing 0.9.3b)
breadboards: 1

parts:
  Part1 = Arduino Uno (Rev3)
  Q1 = pnp-Powertransistor [package="TO220 [THT]"]
  L1 = Solenoid
  D1 = Diode [package=diode-1n4001]
  R1 = Resistor [tolerance=±5% resistance=1k package=THT]

nets:
  N1: Part1.D4, R1.Pin_1
  N2: Q1.base, R1.Pin_0
  N3: Q1.collector, L1.pin1, D1.A
  N4: L1.pin2, D1.C

notes:
  12V 5A DC power supply
